# Fritzing sketch input-force (saved by Fritzing 0.8.7b)
breadboards: 1

parts:
  J1 = Basic Force Sensing Resistor (FSR) [package=THT]
  R1 = Resistor [tolerance=±5% resistance=10k package=THT]

nets:
  N1: J1.pin_0, R1.Pin_0
