# Fritzing sketch output-rgb (saved by Fritzing 0.8.7b)
breadboards: 1

parts:
  R1 = Resistor [tolerance=±5% resistance=560 package=THT]
  LED1 = RGB LED - (4 legs) [package="5 mm [THT]"]
  R2 = Resistor [tolerance=±5% resistance=560 package=THT]
  R3 = Resistor [tolerance=±5% resistance=560 package=THT]

nets:
  N1: R1.Pin_0, LED1.blue_cathode
  N2: LED1.red_cathode, R2.Pin_0
  N3: LED1.common_anode, R3.Pin_0
