# Fritzing sketch output-servo (saved by Fritzing 0.8.7b)
breadboards: 1

parts:
  C1 = Electrolytic Capacitor [capacitance=0.47mF package="200 mil [THT, electrolytic]"]
  J1 = Basic Servo

nets:
  N1: C1.-, J1.gnd
  N2: C1.+, J1.vcc
